// Logisim project AluCris.circ as structural Verilog: 1 circuit, main circuit AluCris
module AluCris (
  input  [15:0] A,
  input  [15:0] B,
  input  [3:0] AluOp,
  output Is_zero,
  output [15:0] Output
);

  wire [15:0] adder_1_out, And_out, Not_out, Or_out, subtractor_1_out;

  Comparator #(.width(16)) comparator_1 (.a({16{1'b0}}), .b(A), .eq(Is_zero));  // open: gt, lt
  assign Or_out = A | B;  // OR_Gate Or, 16 bits wide
  assign And_out = A & B;  // AND_Gate And, 16 bits wide
  Adder #(.width(16)) adder_1 (.a(A), .b(B), .out(adder_1_out));  // open: cin, cout
  Subtractor #(.width(16)) subtractor_1 (.a(A), .b(B), .out(subtractor_1_out));  // open: bin, bout
  assign Not_out = ~A;  // NOT_Gate Not, 16 bits wide
  Multiplexer #(.select(4), .width(16), .enable("false")) multiplexer_1 (
    .in0(Or_out), .in1(And_out), .in2(adder_1_out), .in3(subtractor_1_out), .in4(Not_out), .out(Output),
    .sel(AluOp));  // open: in5, in6, in7, in8, in9, in10, in11, in12, in13, in14, in15
endmodule
