// Logisim project final arqui.circ as structural Verilog: 5 circuits, main circuit main
module main (
);

  wire alu_1_is_zero, undriven, undriven_2, undriven_5, undriven_7, undriven_8, undriven_10, undriven_11;
  wire [3:0] undriven_9;
  wire [7:0] ram_1_data_3;
  wire [11:8] ram_1_data;
  wire [15:0] adder_1_out, alu_1_output, bit_extender_3_out, multiplexer_1_out, multiplexer_2_out,
       multiplexer_3_out, multiplexer_4_out, PC_q, ram_2_data, register_file_1_rd_2, register_file_1_rs,
       register_file_1_rt, undriven_3, undriven_4, undriven_6;
  wire [15:12] ram_1_data_2;

  Adder #(.width(16)) adder_1 (.a(PC_q), .b(multiplexer_1_out), .out(adder_1_out));  // open: cin, cout
  Register #(.width(16)) PC (.D(adder_1_out), .Q(PC_q));  // open: en, clk, clr
  Multiplexer #(.width(16)) multiplexer_1 (
    .in0(undriven_3), .in1(undriven_4), .out(multiplexer_1_out), .sel(undriven_2), .en(undriven));
  RAM #(.addrWidth(16), .dataWidth(16)) ram_1 (
    .addr(PC_q), .data({ram_1_data_2, ram_1_data, ram_1_data_3}));  // open: sel, clk, ld, clr
  Bit_Extender #(.in_width(16), .out_width(8)) bit_extender_1 (.in(undriven_3), .out(ram_1_data_3));
  Bit_Extender #(.in_width(16), .out_width(12)) bit_extender_2 (.in(undriven_4), .out({ram_1_data, ram_1_data_3}));
  Register_File register_file_1 (
    .Data(multiplexer_4_out), .Write_Enable(undriven_5), .rd(ram_1_data), .in_5(ram_1_data_3[3:0]),
    .in_6(ram_1_data_3[7:4]), .rt(register_file_1_rt), .rs(register_file_1_rs), .rd_2(register_file_1_rd_2));  // open: Clock
  assign bit_extender_3_out = {{8{1'b0}}, ram_1_data_3};  // Bit_Extender bit_extender_3
  Multiplexer #(.width(16)) multiplexer_2 (
    .in0(register_file_1_rt), .in1(undriven_6), .out(multiplexer_2_out), .en(undriven_7));  // open: sel
  Multiplexer #(.select(2), .width(16)) multiplexer_3 (
    .in0(register_file_1_rt), .in1(register_file_1_rs), .in2(register_file_1_rd_2), .in3(bit_extender_3_out),
    .out(multiplexer_3_out), .en(undriven_8));  // open: sel
  ALU alu_1 (
    .A(multiplexer_2_out), .B(multiplexer_3_out), .AluOp(undriven_9), .Is_zero(alu_1_is_zero),
    .Output(alu_1_output));
  RAM #(.addrWidth(16), .dataWidth(16), .bus("separate")) ram_2 (
    .addr(alu_1_output), .din(undriven_6), .data(ram_2_data), .str(undriven_10), .ld(undriven_11));  // open: sel, clk, clr
  Multiplexer #(.width(16)) multiplexer_4 (
    .in0(ram_2_data), .in1(alu_1_output), .out(multiplexer_4_out));  // open: sel, en

  // Notes on the sheet:
  //   PCSrc
  //   4
  //   Write rd?
  //   ests 4 bits van al control
  //   rs o st?
  //   alu src
  //   Alu op
  //   zero
  //   Mem read
  //   Mem write
  //   memtoReg
endmodule

module Register_File (
  input  [15:0] Data,
  input  Clock,
  input  Write_Enable,
  input  [3:0] rd,
  input  [3:0] in_5,
  input  [3:0] in_6,
  output [15:0] rt,
  output [15:0] rs,
  output [15:0] rd_2
);

  wire and_1_out, and_3_out, and_4_out, and_5_out, and_6_out, and_7_out, and_8_out, and_9_out, and_10_out,
       and_11_out, and_12_out, and_13_out, and_14_out, and_15_out, and_16_out, and_17_out,
       demultiplexer_1_out0, demultiplexer_1_out1, demultiplexer_1_out2, demultiplexer_1_out3,
       demultiplexer_1_out4, demultiplexer_1_out5, demultiplexer_1_out6, demultiplexer_1_out7,
       demultiplexer_1_out8, demultiplexer_1_out9, demultiplexer_1_out10, demultiplexer_1_out11,
       demultiplexer_1_out12, demultiplexer_1_out13, demultiplexer_1_out14, demultiplexer_1_out15;
  wire [15:0] register_1_q, register_2_q, register_3_q, register_4_q, register_5_q, register_6_q,
       register_7_q, register_8_q, register_9_q, register_10_q, register_11_q, register_12_q, register_13_q,
       register_14_q, register_15_q;

  Demultiplexer #(.select(4), .enable("false")) demultiplexer_1 (
    .out0(demultiplexer_1_out0), .out1(demultiplexer_1_out1), .out2(demultiplexer_1_out2),
    .out3(demultiplexer_1_out3), .out4(demultiplexer_1_out4), .out5(demultiplexer_1_out5),
    .out6(demultiplexer_1_out6), .out7(demultiplexer_1_out7), .out8(demultiplexer_1_out8),
    .out9(demultiplexer_1_out9), .out10(demultiplexer_1_out10), .out11(demultiplexer_1_out11),
    .out12(demultiplexer_1_out12), .out13(demultiplexer_1_out13), .out14(demultiplexer_1_out14),
    .out15(demultiplexer_1_out15), .in(1'b1), .sel(rd));
  and and_1 (and_1_out, Clock, Write_Enable);
  // AND_Gate and_2 has open pins: in1=and_1_out, in2=demultiplexer_1_out0, out=open
  and and_3 (and_3_out, and_1_out, demultiplexer_1_out1);
  and and_4 (and_4_out, and_1_out, demultiplexer_1_out2);
  and and_5 (and_5_out, and_1_out, demultiplexer_1_out3);
  and and_6 (and_6_out, and_1_out, demultiplexer_1_out4);
  and and_7 (and_7_out, and_1_out, demultiplexer_1_out5);
  and and_8 (and_8_out, and_1_out, demultiplexer_1_out6);
  and and_9 (and_9_out, and_1_out, demultiplexer_1_out7);
  and and_10 (and_10_out, and_1_out, demultiplexer_1_out8);
  and and_11 (and_11_out, and_1_out, demultiplexer_1_out9);
  and and_12 (and_12_out, and_1_out, demultiplexer_1_out10);
  and and_13 (and_13_out, and_1_out, demultiplexer_1_out11);
  and and_14 (and_14_out, and_1_out, demultiplexer_1_out12);
  and and_15 (and_15_out, and_1_out, demultiplexer_1_out13);
  and and_16 (and_16_out, and_1_out, demultiplexer_1_out14);
  and and_17 (and_17_out, and_1_out, demultiplexer_1_out15);
  Register #(.width(16)) register_1 (.D(Data), .Q(register_1_q), .clk(and_3_out));  // open: en, clr
  Register #(.width(16)) register_2 (.D(Data), .Q(register_2_q), .clk(and_4_out));  // open: en, clr
  Register #(.width(16)) register_3 (.D(Data), .Q(register_3_q), .clk(and_5_out));  // open: en, clr
  Register #(.width(16)) register_4 (.D(Data), .Q(register_4_q), .clk(and_6_out));  // open: en, clr
  Register #(.width(16)) register_5 (.D(Data), .Q(register_5_q), .clk(and_7_out));  // open: en, clr
  Register #(.width(16)) register_6 (.D(Data), .Q(register_6_q), .clk(and_8_out));  // open: en, clr
  Register #(.width(16)) register_7 (.D(Data), .Q(register_7_q), .clk(and_9_out));  // open: en, clr
  Register #(.width(16)) register_8 (.D(Data), .Q(register_8_q), .clk(and_10_out));  // open: en, clr
  Register #(.width(16)) register_9 (.D(Data), .Q(register_9_q), .clk(and_11_out));  // open: en, clr
  Register #(.width(16)) register_10 (.D(Data), .Q(register_10_q), .clk(and_12_out));  // open: en, clr
  Register #(.width(16)) register_11 (.D(Data), .Q(register_11_q), .clk(and_13_out));  // open: en, clr
  Register #(.width(16)) register_12 (.D(Data), .Q(register_12_q), .clk(and_14_out));  // open: en, clr
  Register #(.width(16)) register_13 (.D(Data), .Q(register_13_q), .clk(and_15_out));  // open: en, clr
  Register #(.width(16)) register_14 (.D(Data), .Q(register_14_q), .clk(and_16_out));  // open: en, clr
  Register #(.width(16)) register_15 (.D(Data), .Q(register_15_q), .clk(and_17_out));  // open: en, clr
  Multiplexer #(.select(4), .width(16), .enable("false")) multiplexer_1 (
    .in0({16{1'b0}}), .in1(register_1_q), .in2(register_2_q), .in3(register_3_q), .in4(register_4_q),
    .in5(register_5_q), .in6(register_6_q), .in7(register_7_q), .in8(register_8_q), .in9(register_9_q),
    .in10(register_10_q), .in11(register_11_q), .in12(register_12_q), .in13(register_13_q),
    .in14(register_14_q), .in15(register_15_q), .out(rt), .sel(in_5));
  Multiplexer #(.select(4), .width(16), .enable("false")) multiplexer_2 (
    .in0({16{1'b0}}), .in1(register_1_q), .in2(register_2_q), .in3(register_3_q), .in4(register_4_q),
    .in5(register_5_q), .in6(register_6_q), .in7(register_7_q), .in8(register_8_q), .in9(register_9_q),
    .in10(register_10_q), .in11(register_11_q), .in12(register_12_q), .in13(register_13_q),
    .in14(register_14_q), .in15(register_15_q), .out(rs), .sel(in_6));
  Multiplexer #(.select(4), .width(16), .enable("false")) multiplexer_3 (
    .in0({16{1'b0}}), .in1(register_1_q), .in2(register_2_q), .in3(register_3_q), .in4(register_4_q),
    .in5(register_5_q), .in6(register_6_q), .in7(register_7_q), .in8(register_8_q), .in9(register_9_q),
    .in10(register_10_q), .in11(register_11_q), .in12(register_12_q), .in13(register_13_q),
    .in14(register_14_q), .in15(register_15_q), .out(rd_2), .sel(rd));
endmodule

module ALU (
  input  [15:0] A,
  input  [15:0] B,
  input  [3:0] AluOp,
  output Is_zero,
  output [15:0] Output
);

  wire [15:0] adder_1_out, And_out, Not_out, Or_out, subtractor_1_out;

  Comparator #(.width(16)) comparator_1 (.a({16{1'b0}}), .b(A), .eq(Is_zero));  // open: gt, lt
  assign Or_out = A | B;  // OR_Gate Or, 16 bits wide
  assign And_out = A & B;  // AND_Gate And, 16 bits wide
  Adder #(.width(16)) adder_1 (.a(A), .b(B), .out(adder_1_out));  // open: cin, cout
  Subtractor #(.width(16)) subtractor_1 (.a(A), .b(B), .out(subtractor_1_out));  // open: bin, bout
  assign Not_out = ~A;  // NOT_Gate Not, 16 bits wide
  Multiplexer #(.select(4), .width(16), .enable("false")) multiplexer_1 (
    .in0(Or_out), .in1(And_out), .in2(adder_1_out), .in3(subtractor_1_out), .in4(Not_out), .out(Output),
    .sel(AluOp));  // open: in5, in6, in7, in8, in9, in10, in11, in12, in13, in14, in15
endmodule

module main_1 (
);

  wire alu_1_is_zero, clock_1_out, control_1_alusrcabajo, control_1_branch, control_1_memread,
       control_1_memtoreg, control_1_memwrite, control_1_regwrite, or_1_out;
  wire [1:0] control_1_pcsrc;
  wire [3:0] control_1_alu_operation;
  wire [11:0] ram_1_data;
  wire [15:0] adder_1_out, alu_1_output, bit_extender_1_out, bit_extender_2_out, bit_extender_3_out,
       multiplexer_1_out, multiplexer_2_out, multiplexer_3_out, multiplexer_4_out, multiplexer_5_out,
       multiplexer_6_out, PC_q, ram_2_data, register_file_1_rd_2, register_file_1_rs, register_file_1_rt;
  wire [15:12] ram_1_data_2;

  Multiplexer #(.select(2), .width(16), .enable("false")) multiplexer_1 (
    .in0(16'h1), .in1(multiplexer_2_out), .in2(multiplexer_3_out), .in3(bit_extender_2_out),
    .out(multiplexer_1_out), .sel(control_1_pcsrc));
  Register #(.width(16), .trigger("falling")) PC (.D(adder_1_out), .Q(PC_q), .clk(clock_1_out));  // open: en, clr
  Adder #(.width(16)) adder_1 (.a(PC_q), .b(multiplexer_1_out), .out(adder_1_out));  // open: cin, cout
  Multiplexer #(.width(16), .enable("false")) multiplexer_2 (
    .in0(16'h1), .in1(bit_extender_1_out), .out(multiplexer_2_out), .sel(alu_1_is_zero));
  Multiplexer #(.width(16), .enable("false")) multiplexer_3 (
    .in0(bit_extender_1_out), .in1(16'h1), .out(multiplexer_3_out), .sel(alu_1_is_zero));
  RAM #(.addrWidth(16), .dataWidth(16)) ram_1 (
    .addr(PC_q), .data({ram_1_data_2, ram_1_data}), .clk(clock_1_out));  // open: sel, ld, clr
  assign bit_extender_1_out = {{8{ram_1_data[7]}}, ram_1_data[7:0]};  // Bit_Extender bit_extender_1
  assign bit_extender_2_out = {{4{ram_1_data[11]}}, ram_1_data};  // Bit_Extender bit_extender_2
  control control_1 (
    .Operation(ram_1_data_2), .Alu_Operation(control_1_alu_operation), .Branch(control_1_branch),
    .MemRead(control_1_memread), .MemWrite(control_1_memwrite), .MemtoReg(control_1_memtoreg),
    .RegWrite(control_1_regwrite), .AluSrcAbajo(control_1_alusrcabajo), .PCSrc(control_1_pcsrc));  // open: RegDest
  Clock clock_1 (.out(clock_1_out));
  Register_File register_file_1 (
    .Data(multiplexer_5_out), .Clock(clock_1_out), .Write_Enable(control_1_regwrite), .rd(ram_1_data[11:8]),
    .in_5(ram_1_data[3:0]), .in_6(ram_1_data[7:4]), .rt(register_file_1_rt), .rs(register_file_1_rs),
    .rd_2(register_file_1_rd_2));
  assign bit_extender_3_out = {{8{ram_1_data[7]}}, ram_1_data[7:0]};  // Bit_Extender bit_extender_3
  Multiplexer #(.width(16), .enable("false")) multiplexer_4 (
    .in0(register_file_1_rs), .in1(register_file_1_rd_2), .out(multiplexer_4_out), .sel(or_1_out));
  or or_1 (or_1_out, control_1_branch, control_1_alusrcabajo);
  Multiplexer #(.width(16)) multiplexer_5 (
    .in0(alu_1_output), .in1(ram_2_data), .out(multiplexer_5_out), .sel(control_1_memtoreg));  // open: en
  Multiplexer #(.width(16), .enable("false")) multiplexer_6 (
    .in0(register_file_1_rt), .in1(bit_extender_3_out), .out(multiplexer_6_out), .sel(control_1_alusrcabajo));
  ALU alu_1 (
    .A(multiplexer_4_out), .B(multiplexer_6_out), .AluOp(control_1_alu_operation), .Is_zero(alu_1_is_zero),
    .Output(alu_1_output));
  RAM #(.addrWidth(16), .dataWidth(16), .bus("separate")) ram_2 (
    .addr(alu_1_output), .din(register_file_1_rd_2), .data(ram_2_data), .str(control_1_memwrite),
    .clk(clock_1_out), .ld(control_1_memread));  // open: sel, clr

  // Notes on the sheet:
  //   PCSrc
  //   Write rd?
  //   ests 4 bits van al control
  //   rs o st?
  //   alu src
  //   MemtoReg
  //   Alu op
  //   zero
  //   branch
  //   Mem read
  //   Mem write
endmodule

module control (
  input  [3:0] Operation,
  output [3:0] Alu_Operation,
  output Branch,
  output MemRead,
  output MemWrite,
  output MemtoReg,
  output RegWrite,
  output RegDest,
  output AluSrcAbajo,
  output [1:0] PCSrc
);

  ROM #(.addrWidth(4), .dataWidth(13)) rom_1 (
    .addr(Operation),
    .data({PCSrc, AluSrcAbajo, RegDest, RegWrite, MemtoReg, MemWrite, MemRead, Branch, Alu_Operation}));  // open: sel

  // Notes on the sheet:
  //   PcSrc
  //   00: PC+1
  //   01: BZ
  //   10: BNZ
  //   11: Jump
  //   2. AluOp2
  //   3. AluOp3
  //   4. AluOp4
  //   5. Branch
  //   6. MemRead
  //   7. MemWrite
  //   contents of rom_1 (hex, n*v repeats v):
  //   302 303 1a2 42 301 300 304 0 702 7ff 810 1010 0 0 0 1810
  //   From right to left:
  //   1. AluOp1
  //   10. RegDst
  //   11. AluSrcAbajo
  //   12. PCSrc
  //   13. PCSrc
  //   8. MemtoReg
  //   9. RegWrite
endmodule
